// Logisim project ex2.circ as structural Verilog: 1 circuit, main circuit compute_BrUn
module compute_BrUn (
  input  [31:0] INSTRUCTION,
  output BrUn
);

  wire comparator_1_eq, comparator_1_gt;

  Comparator #(.mode("unsigned"), .width(3)) comparator_1 (
    .a(INSTRUCTION[14:12]), .b(3'b110), .gt(comparator_1_gt), .eq(comparator_1_eq));  // open: lt
  or or_1 (BrUn, comparator_1_gt, comparator_1_eq);
endmodule
